// Logisim project TTY_Controller.circ as structural Verilog: 4 circuits, main circuit TTY_Main
module TTY_Main (
  input  [6:0] Ctrl_Down,
  input  [31:0] Data_In,
  input  [31:0] Addr_In,
  output [31:0] Addr_To_RAM,
  output [1:0] Ctrl_Up,
  output [31:0] Data_Out,
  output Clk,
  output En_Write,
  output Clear,
  output [6:0] Data
);

  wire IRQ, msi_sys_1_bus_req, msi_sys_1_msi, or_1_out, tlp_receptor_1_dma_ack, tlp_receptor_1_ecam,
       tlp_receptor_1_en_read_cpu, tlp_receptor_1_en_write_cpu, tlp_receptor_1_mmio, tlp_receptor_1_rst,
       tty_controller_1_bus_req, tty_controller_1_clean_regs;
  wire [15:0] endpoint_ecam_1_comand, M_Config, tty_controller_1_status;
  wire [31:0] endpoint_ecam_1_bar_out_0, endpoint_ecam_1_data_out, MA, MD, msi_sys_1_addr,
       msi_sys_1_data_out, multiplexer_2_out, registers_bar0_tty_1_cant_out, registers_bar0_tty_1_comand_out,
       registers_bar0_tty_1_data_out, registers_bar0_tty_1_length_out, registers_bar0_tty_1_w_a,
       tty_controller_1_addr_to_ram;

  TLP_Receptor tlp_receptor_1 (
    .Bus_REQ(or_1_out), .En_Write(msi_sys_1_msi), .Ctrl_Downstream(Ctrl_Down), .ECAM(tlp_receptor_1_ecam),
    .MMIO(tlp_receptor_1_mmio), .En_Write_CPU(tlp_receptor_1_en_write_cpu),
    .En_Read_CPU(tlp_receptor_1_en_read_cpu), .DMA_ACK(tlp_receptor_1_dma_ack), .Clk(Clk),
    .RST(tlp_receptor_1_rst), .Ctrl_Upstream(Ctrl_Up));
  EndPoint_ECAM endpoint_ecam_1 (
    .Is_ECAM(tlp_receptor_1_ecam), .RST(tlp_receptor_1_rst), .Clk(Clk), .Data_In(Data_In), .Addr(Addr_In),
    .Read(tlp_receptor_1_en_read_cpu), .Write(tlp_receptor_1_en_write_cpu), .Status(tty_controller_1_status),
    .Vendor_Device(32'h7a320003), .Class_Code(24'h70000), .Header_Type({8{1'b0}}), .ERBA({32{1'b1}}),
    .In_BAR_0(32'hf), .In_BAR_1({32{1'b0}}), .In_BAR_2({32{1'b0}}), .In_BAR_3({32{1'b0}}),
    .Next_Pointer({8{1'b1}}), .MSI_Cant(3'b000), .Data_Out(endpoint_ecam_1_data_out),
    .Comand(endpoint_ecam_1_comand), .M_Config(M_Config), .MA(MA), .MD(MD),
    .BAR_Out_0(endpoint_ecam_1_bar_out_0));  // open: BAR_Out_1, BAR_Out_2, BAR_Out_3
  Multiplexer #(.width(32)) multiplexer_1 (
    .in0(tty_controller_1_addr_to_ram), .in1(msi_sys_1_addr), .out(Addr_To_RAM), .sel(msi_sys_1_msi));
  Registers_BAR0_TTY registers_bar0_tty_1 (
    .BAR_0(endpoint_ecam_1_bar_out_0), .BAR_0_REQ(32'hf), .MMIO(tlp_receptor_1_mmio),
    .Ctrl(endpoint_ecam_1_comand), .Clean_Reg(tty_controller_1_clean_regs), .RST(tlp_receptor_1_rst),
    .Clk(Clk), .Read(tlp_receptor_1_en_read_cpu), .Write(tlp_receptor_1_en_write_cpu), .Data_In(Data_In),
    .Addr(Addr_In), .Data_Out(registers_bar0_tty_1_data_out), .Comand_Out(registers_bar0_tty_1_comand_out),
    .W_A(registers_bar0_tty_1_w_a), .Length_Out(registers_bar0_tty_1_length_out),
    .Cant_Out(registers_bar0_tty_1_cant_out));
  Multiplexer #(.enable("true"), .width(32)) multiplexer_2 (
    .in0(endpoint_ecam_1_data_out), .in1(registers_bar0_tty_1_data_out), .out(multiplexer_2_out),
    .sel(tlp_receptor_1_mmio), .en(tlp_receptor_1_en_read_cpu));
  or or_1 (or_1_out, msi_sys_1_bus_req, tty_controller_1_bus_req);
  TTY_Controller tty_controller_1 (
    .Comand(registers_bar0_tty_1_comand_out), .W_A(registers_bar0_tty_1_w_a),
    .DMA_ACK(tlp_receptor_1_dma_ack), .RST(tlp_receptor_1_rst), .Clk(Clk),
    .Cant(registers_bar0_tty_1_cant_out), .Length(registers_bar0_tty_1_length_out),
    .Ctrl(endpoint_ecam_1_comand), .Data_From_RAM(Data_In), .Status(tty_controller_1_status),
    .Clean_Regs(tty_controller_1_clean_regs), .IRQ(IRQ), .Addr_To_RAM(tty_controller_1_addr_to_ram),
    .Data_Out(Data), .Write_En(En_Write), .Clear(Clear), .Bus_REQ(tty_controller_1_bus_req));
  Multiplexer #(.width(32)) multiplexer_3 (
    .in0(multiplexer_2_out), .in1(msi_sys_1_data_out), .out(Data_Out), .sel(msi_sys_1_msi));
  MSI_Sys msi_sys_1 (
    .M_config(M_Config), .Code({5{1'b0}}), .MD(MD), .MA(MA), .DMA_ACK(tlp_receptor_1_dma_ack), .IRQ(IRQ),
    .Addr(msi_sys_1_addr), .MSI(msi_sys_1_msi), .Bus_REQ(msi_sys_1_bus_req), .Data_Out(msi_sys_1_data_out));
endmodule

module TLP_Receptor (
  input  [6:0] Ctrl_Downstream,
  input  Bus_REQ,
  input  En_Write,
  output ECAM,
  output MMIO,
  output En_Write_CPU,
  output En_Read_CPU,
  output DMA_ACK,
  output Clk,
  output RST,
  output [1:0] Ctrl_Upstream
);


  assign Clk = Ctrl_Downstream[5];
  assign Ctrl_Upstream = {En_Write, Bus_REQ};
  assign DMA_ACK = Ctrl_Downstream[4];
  assign ECAM = Ctrl_Downstream[0];
  assign En_Read_CPU = Ctrl_Downstream[3];
  assign En_Write_CPU = Ctrl_Downstream[2];
  assign MMIO = Ctrl_Downstream[1];
  assign RST = Ctrl_Downstream[6];
endmodule

module TTY_Controller (
  input  [15:0] Ctrl,
  input  [31:0] Comand,
  input  Clk,
  input  RST,
  input  [31:0] W_A,
  input  [31:0] Data_From_RAM,
  input  [31:0] Cant,
  input  [31:0] Length,
  input  DMA_ACK,
  output [15:0] Status,
  output Clean_Regs,
  output Write_En,
  output Clear,
  output Bus_REQ,
  output [31:0] Addr_To_RAM,
  output [6:0] Data_Out,
  output IRQ
);

  wire and_1_out, and_2_out, and_3_out, and_4_out, and_6_out, and_7_out, and_9_out, counter_1_carry,
       d_ff_1_q, Error, Finish, or_1_out, or_2_out, or_3_out, or_4_out, Starting;
  wire [1:0] pla_4_out, pla_5_out;
  wire [2:0] bit_extender_1_out, multiplexer_1_out, register_1_q;
  wire [2:1] pla_1_out;
  wire [3:1] pla_3_out;
  wire [6:0] bit_extender_2_out, bit_extender_3_out;
  wire [31:0] adder_1_out, multiplexer_2_out, multiplexer_3_out;

  Bit_Extender #(.in_width(32), .out_width(3), .\type ("zero")) bit_extender_1 (.in(Comand), .out(bit_extender_1_out));
  and and_1 (and_1_out, Starting, ~Clean_Regs);  // AND_Gate
  or or_1 (or_1_out, RST, Error, Finish);
  Adder #(.width(32)) adder_1 (.a(Addr_To_RAM), .b(32'h1), .out(adder_1_out));  // open: cin, cout
  and and_2 (and_2_out, Starting, ~Clean_Regs);  // AND_Gate
  and and_3 (and_3_out, DMA_ACK, Bus_REQ, Starting, ~Clear);  // AND_Gate
  and and_4 (and_4_out, ~Clear, Starting, ~DMA_ACK, ~Bus_REQ);  // AND_Gate
  PLA #(.in_width(5), .out_width(1), .\table ("10001 1 # Write A")) pla_1 (
    .in({multiplexer_1_out, Ctrl[1:0]}), .out(pla_1_out[1]));
  Multiplexer #(.width(3)) multiplexer_1 (
    .in0(bit_extender_1_out), .in1(register_1_q), .out(multiplexer_1_out), .sel(Clean_Regs));
  Register #(.width(3)) register_1 (
    .D(bit_extender_1_out), .en(and_1_out), .Q(register_1_q), .clk(Clk), .clr(or_1_out));
  Multiplexer #(.width(32)) multiplexer_2 (.in0(W_A), .in1(adder_1_out), .out(multiplexer_2_out), .sel(Clean_Regs));
  or or_2 (or_2_out, and_2_out, and_3_out);
  Multiplexer #(.width(32)) multiplexer_3 (.in0(Cant), .in1(Length), .out(multiplexer_3_out), .sel(Bus_REQ));
  or or_3 (or_3_out, and_3_out, and_4_out);
  PLA #(.in_width(5), .out_width(1), .\table ("001x1 1 # Write\n010x1 1 # Delete\n011x1 1 # Clear\n100x1 1 # Write A\n000x1 1 # NOP\nxxxx0 1 # OFF")) pla_2 (
    .in({multiplexer_1_out, Ctrl[1:0]}), .out(pla_1_out[2]));
  PLA #(.in_width(5), .out_width(5), .\table ("001x1 00011 # Write\n010x1 00101 # Delete\n011x1 01001 # Clear\n10011 10001 # Write A")) pla_3 (
    .in({multiplexer_1_out, Ctrl[1:0]}), .out({Bus_REQ, pla_3_out, Starting}));
  Register #(.width(32)) register_2 (.D(multiplexer_2_out), .en(or_2_out), .Q(Addr_To_RAM), .clk(Clk), .clr(or_1_out));
  Counter #(.max('hffffffff), .width(32)) counter_1 (
    .load(and_2_out), .D(multiplexer_3_out), .count(or_3_out), .carry(counter_1_carry), .up(and_2_out),
    .clk(Clk), .clr(or_1_out));  // open: Q
  PLA #(.in_width(3), .out_width(3), .\table ("100 000 # Ready\n101 001 # Busy\n0xx 110 # Innvalid\n11x 111 # Not DMA")) pla_4 (
    .in({pla_1_out, Clean_Regs}), .out({Error, pla_4_out}));
  PLA #(.in_width(5), .\table ("00011 00 # Write\n00101 01 # Delete\n10001 10 # Write A")) pla_5 (
    .in({Bus_REQ, pla_3_out, Starting}), .out(pla_5_out));
  Bit_Extender #(.in_width(32), .out_width(7), .\type ("zero")) bit_extender_2 (
    .in(Addr_To_RAM), .out(bit_extender_2_out));
  Bit_Extender #(.in_width(32), .out_width(7), .\type ("zero")) bit_extender_3 (
    .in(Data_From_RAM), .out(bit_extender_3_out));
  and and_5 (Finish, Write_En, counter_1_carry);
  assign Status = {{14{1'b0}}, pla_4_out};  // Bit_Extender bit_extender_4
  and and_6 (and_6_out, ~Clear, Clean_Regs);  // AND_Gate
  and and_7 (and_7_out, ~and_6_out, Starting);  // AND_Gate
  or or_4 (or_4_out, pla_3_out[1], pla_3_out[2], Bus_REQ);
  Multiplexer #(.enable("true"), .select(2), .width(7)) multiplexer_4 (
    .in0(bit_extender_2_out), .in1(7'b0001000), .in2(bit_extender_3_out), .out(Data_Out), .sel(pla_5_out),
    .en(Write_En));  // open: in3
  T_Flip_Flop t_ff_1 (.T(and_7_out), .clk(Clk), .Q(Clean_Regs), .reset(or_1_out));  // open: Qn, preset
  D_Flip_Flop d_ff_1 (.D(Clean_Regs), .clk(Clk), .Q(d_ff_1_q));  // open: Qn, preset, reset
  and and_8 (Write_En, or_4_out, Clean_Regs);
  and and_9 (and_9_out, pla_3_out[3], Clean_Regs);
  and and_10 (IRQ, d_ff_1_q, ~Clean_Regs);  // AND_Gate
  or or_5 (Clear, and_9_out, RST);

  // Other names for the same wires on the sheet: Busy = Clean_Regs; Write_A = Bus_REQ; Write = Write_En

  // Notes on the sheet:
  //   Finish Detector
endmodule

module Registers_BAR0_TTY (
  input  [31:0] Addr,
  input  Clean_Reg,
  input  RST,
  input  Clk,
  input  Read,
  input  Write,
  input  [31:0] Data_In,
  input  MMIO,
  input  [15:0] Ctrl,
  input  [31:0] BAR_0,
  input  [31:0] BAR_0_REQ,
  output [31:0] Data_Out,
  output [31:0] Comand_Out,
  output [31:0] W_A,
  output [31:0] Length_Out,
  output [31:0] Cant_Out
);

  wire and_1_out, and_2_out, and_3_out, and_5_out, comparator_1_eq, comparator_1_gt, comparator_2_eq,
       comparator_2_gt, decoder_1_out0, decoder_1_out1, decoder_1_out2, decoder_1_out3, Enable, or_1_out,
       or_2_out, or_3_out;
  wire [31:0] adder_1_out;

  Adder #(.width(32)) adder_1 (.a(BAR_0), .b(BAR_0_REQ), .out(adder_1_out));  // open: cin, cout
  or or_1 (or_1_out, Clean_Reg, RST);
  and and_1 (and_1_out, Read, Enable);
  and and_2 (and_2_out, Enable, Write);
  Decoder #(.select(2)) decoder_1 (
    .out0(decoder_1_out0), .out1(decoder_1_out1), .out2(decoder_1_out2), .out3(decoder_1_out3),
    .sel(Addr[3:2]), .en(and_2_out));
  and and_3 (and_3_out, MMIO, Ctrl[0]);
  or or_2 (or_2_out, comparator_1_gt, comparator_1_eq);
  Comparator #(.mode("unsigned"), .width(32)) comparator_1 (
    .a(Addr), .b(BAR_0), .gt(comparator_1_gt), .eq(comparator_1_eq));  // open: lt
  or or_3 (or_3_out, comparator_2_gt, comparator_2_eq);
  Comparator #(.mode("unsigned"), .width(32)) comparator_2 (
    .a(adder_1_out), .b(Addr), .gt(comparator_2_gt), .eq(comparator_2_eq));  // open: lt
  and and_4 (Enable, and_3_out, and_5_out);
  and and_5 (and_5_out, or_2_out, or_3_out);
  Register #(.width(32)) Comand (.D(Data_In), .en(decoder_1_out0), .clk(Clk), .Q(Comand_Out), .clr(or_1_out));
  Register #(.width(32)) Word_Addr (.D(Data_In), .en(decoder_1_out1), .clk(Clk), .Q(W_A), .clr(or_1_out));
  Register #(.width(32)) Length (.D(Data_In), .en(decoder_1_out2), .clk(Clk), .Q(Length_Out), .clr(or_1_out));
  Register #(.width(32)) Cant (.D(Data_In), .en(decoder_1_out3), .clk(Clk), .Q(Cant_Out), .clr(or_1_out));
  Multiplexer #(.enable("true"), .select(2), .width(32)) multiplexer_1 (
    .in0(Comand_Out), .in1(W_A), .in2(Length_Out), .in3(Cant_Out), .out(Data_Out), .sel(Addr[3:2]),
    .en(and_1_out));
endmodule
