// Logisim project Main_Memories.circ as structural Verilog: 2 circuits, main circuit Memory
module Memory (
  input  [31:0] Addr,
  input  RST,
  input  Read_En,
  input  [7:0] Write_Flags,
  input  Clk,
  input  [31:0] Data_In,
  input  Write_En,
  output RAM_Ready,
  output [63:0] out_9
);

  wire decoder_1_out0, decoder_1_out1, decoder_1_out2, decoder_1_out3;
  wire [7:0] ram_1_p5, ram_1_p6, ram_1_p7, ram_1_p8, ram_1_p9, ram_1_p10, ram_1_p11, ram_1_p12, ram_2_p5,
       ram_3_p5, ram_3_p6, ram_3_p7, ram_3_p8, ram_3_p9, ram_3_p10, ram_3_p11, ram_3_p12, ram_4_p5, ram_4_p6,
       ram_4_p7, ram_4_p8, ram_4_p9, ram_4_p10, ram_4_p11, ram_4_p12, undriven, undriven_2, undriven_3,
       undriven_4, undriven_5, undriven_6, undriven_7;

  Decoder #(.select(2)) decoder_1 (
    .out0(decoder_1_out0), .out1(decoder_1_out1), .out2(decoder_1_out2), .out3(decoder_1_out3),
    .sel(Addr[31:30]), .en(Write_En));
  // RAM #(.addrWidth(30), .clearpin("true"), .enables("line"), .line("octo"), .misaligned("true")) ram_1: pin names not known; wires that end beside it: Addr[29:0], decoder_1_out3, Clk, RST, ram_1_p5, ram_1_p6, ram_1_p7, ram_1_p8, ram_1_p9, ram_1_p10, ram_1_p11, ram_1_p12
  // RAM #(.addrWidth(30), .clearpin("true"), .enables("line"), .line("octo"), .misaligned("true")) ram_2: pin names not known; wires that end beside it: Addr[29:0], decoder_1_out0, Clk, RST, ram_2_p5
  // RAM #(.addrWidth(30), .clearpin("true"), .enables("line"), .line("octo"), .misaligned("true")) ram_3: pin names not known; wires that end beside it: Addr[29:0], decoder_1_out1, Clk, RST, ram_3_p5, ram_3_p6, ram_3_p7, ram_3_p8, ram_3_p9, ram_3_p10, ram_3_p11, ram_3_p12
  // RAM #(.addrWidth(30), .clearpin("true"), .enables("line"), .line("octo"), .misaligned("true")) ram_4: pin names not known; wires that end beside it: Addr[29:0], decoder_1_out2, Clk, RST, ram_4_p5, ram_4_p6, ram_4_p7, ram_4_p8, ram_4_p9, ram_4_p10, ram_4_p11, ram_4_p12
  Multiplexer #(.enable("true"), .select(2), .width(64)) multiplexer_1 (
    .in0({ram_3_p11, ram_3_p10, ram_3_p9, ram_3_p8, ram_3_p7, ram_3_p6, ram_3_p5, ram_2_p5}),
    .in1({ram_4_p11, ram_4_p10, ram_4_p9, ram_4_p8, ram_4_p7, ram_4_p6, ram_4_p5, ram_3_p12}),
    .in2({undriven_7, undriven_6, undriven_5, undriven_4, undriven_3, undriven_2, undriven, ram_4_p12}),
    .in3({ram_1_p12, ram_1_p11, ram_1_p10, ram_1_p9, ram_1_p8, ram_1_p7, ram_1_p6, ram_1_p5}), .out(out_9),
    .sel(Addr[31:30]), .en(Read_En));

  assign RAM_Ready = 1'b1;

  // Other names for the same wires on the sheet: Sel[1:0] = Addr[31:30]
endmodule

module ROM_BIOS (
  input  [19:0] Addr,
  output [63:0] Data_Out
);

  // ROM #(.addrWidth(20), .line("octo"), .misaligned("true")) rom_1: pin names not known; wires that end beside it: Addr, Data_Out[31:24], Data_Out[23:16], Data_Out[15:8], Data_Out[7:0], Data_Out[63:56], Data_Out[55:48], Data_Out[47:40], Data_Out[39:32]

  // Notes on the sheet:
  //   contents of rom_1 (hex, n*v repeats v):
  //   d e0 0 38 53 e8 0 14 53 e9 0 10 53 ea 0 c 53 eb 0 8 53 ec 0 4 53 ed 0 0 53 e4 0 24 82 20 60 0 82 10
  //   70 0 c 10 0 ff 3 17 0 0 8c f0 ff f0 8d f0 0 48 f 4f 0 0 8c f0 ff f0 8d f0 0 68 e f 0 0 52 ed 0 0 52
  //   ec 0 4 52 eb 0 8 52 ea 0 c 52 e9 0 10 52 e8 0 14 d e0 ff c8 11 0 0 0 c 10 0 14 a 71 10 0 6 11 10 0 c
  //   20 0 0 8c 20 e0 0 8d 20 0 0 6 22 20 0 6 12 10 0 53 e1 0 34 c 90 0 0 c 80 ff ff c d0 0 0 8c d0 c0 0
  //   8d d0 0 0 c 40 0 18 c a0 0 10 53 e9 0 1c 53 e3 0 28 53 e6 0 2c 53 e7 0 20 53 e5 0 30 52 eb 0 34 82
  //   90 20 0 52 b1 0 0 7 18 10 0 3 18 0 0 8c f0 ff f0 8d f0 6 c8 f f 0 0 8c f0 ff f0 8d f0 0 e8 e f 0 0
  //   53 e2 0 18 52 31 0 0 c 20 0 3f 3 21 0 0 8c f0 ff f0 8d f0 0 48 f 2f 0 0 8c f0 ff f0 8d f0 1 10 e f 0
  //   0 c 20 0 13 4 12 10 0 2 61 c0 0 52 51 0 0 2 1d 10 0 9 14 20 0 13 c2 0 3 9 1a 20 0 13 c2 0 2 13 c1 0
  //   0 c 20 0 8 82 60 80 0 82 20 60 0 9 16 10 0 13 c1 0 1 13 c7 0 10 52 e1 0 1c 13 c1 0 11 52 e1 0 18 13
  //   c1 0 12 52 b1 0 8 9 14 20 0 13 c2 0 f 9 1a 20 0 13 c2 0 e 13 c1 0 c 9 16 10 0 13 c1 0 d 52 b1 0 8 9
  //   14 10 0 c 60 0 7f 7 16 10 0 c 60 0 1 3 16 0 0 8c f0 ff f0 8d f0 4 64 f f 0 0 8c f0 ff f0 8d f0 1 b0
  //   e f 0 0 82 80 60 0 c 80 ff ff 3 19 0 0 8c f0 ff f0 8d f0 7 74 f 1f 0 0 8c f0 ff f0 8d f0 1 d4 e f 0
  //   0 c 10 0 0 8c 10 0 0 8d 10 ff ff 53 b1 10 0 52 b1 10 0 82 60 70 0 3 19 0 0 8c f0 ff f0 8d f0 2 4c f
  //   f 0 0 8c f0 ff f0 8d f0 2 8 e f 0 0 52 52 0 0 2 2d 20 0 53 b2 10 0 c 60 10 0 82 60 20 0 3 61 0 0 8c
  //   f0 ff f0 8d f0 2 2c f 4f 0 0 d 10 f ff c 20 0 0 8c 20 0 0 8d 20 f0 0 7 12 20 0 52 51 0 0 2 12 10 0
  //   53 51 0 0 c 10 0 0 8c 10 0 0 8d 10 ff ff 53 b1 10 4 52 b1 10 4 3 19 0 0 8c f0 ff f0 8d f0 2 c0 f f 0
  //   0 8c f0 ff f0 8d f0 2 7c e f 0 0 52 52 0 0 2 2d 20 0 53 b2 10 4 c 60 10 0 82 60 20 0 3 61 0 0 8c f0
  //   ff f0 8d f0 2 a0 f 4f 0 0 d 10 f ff c 20 0 0 8c 20 0 0 8d 20 f0 0 7 12 20 0 52 51 0 0 2 12 10 0 53
  //   51 0 0 c 10 0 0 8c 10 0 0 8d 10 ff ff 53 b1 10 8 52 b1 10 8 3 19 0 0 8c f0 ff f0 8d f0 3 34 f f 0 0
  //   8c f0 ff f0 8d f0 2 f0 e f 0 0 52 52 0 0 2 2d 20 0 53 b2 10 8 c 60 10 0 82 60 20 0 3 61 0 0 8c f0 ff
  //   f0 8d f0 3 14 f 4f 0 0 d 10 f ff c 20 0 0 8c 20 0 0 8d 20 f0 0 7 12 20 0 52 51 0 0 2 12 10 0 53 51 0
  //   0 c 10 0 0 8c 10 0 0 8d 10 ff ff 53 b1 10 c 52 b1 10 c 3 19 0 0 8c f0 ff f0 8d f0 3 64 f 1f 0 0 8c
  //   f0 ff f0 8d f0 7 38 e f 0 0 52 52 0 0 2 2d 20 0 53 b2 10 c c 20 10 1 3 12 0 0 8c f0 ff f0 8d f0 3 90
  //   f 4f 0 0 8c f0 ff f0 8d f0 7 48 e f 0 0 52 51 0 0 d 10 10 0 53 51 0 0 12 c2 0 2 a 2a 20 0 6 22 20 0
  //   12 c6 0 3 a 64 40 0 6 44 40 0 6 42 20 0 12 c8 0 1 c 40 0 8 82 40 60 0 a 86 40 0 6 44 80 0 12 c4 0 0
  //   6 44 40 0 6 84 80 0 c 40 0 18 6 22 20 0 6 88 80 0 6 28 20 0 3 12 10 0 c d0 0 0 8c d0 c0 0 8d d0 0 0
  //   2 1d 10 0 9 1a 20 0 13 c2 0 a 9 14 20 0 13 c2 0 b 13 c1 0 8 9 16 10 0 13 c1 0 9 52 51 0 0 2 1d 10 0
  //   9 14 20 0 13 c2 0 7 9 1a 20 0 13 c2 0 6 13 c1 0 4 9 16 10 0 13 c1 0 5 52 31 0 0 d 10 0 1 53 31 0 0
  //   52 e2 0 18 82 70 60 0 52 e7 0 20 c 80 ff ff 8c f0 ff f0 8d f0 6 c8 e f 0 0 82 30 60 0 52 61 0 0 d 10
  //   0 1 53 61 0 0 52 e9 0 24 52 91 0 0 52 b2 10 0 c 30 0 0 8c 30 ff 0 8d 30 0 0 7 23 20 0 6 22 20 0 a 1a
  //   30 0 c d0 0 0 8c d0 0 ff 8d d0 0 0 7 3d 30 0 6 33 30 0 6 32 20 0 6 77 30 0 6 22 20 0 6 23 20 0 53 b2
  //   10 0 c 20 0 ff 7 12 d0 0 52 91 0 0 d 10 0 1 53 91 0 0 82 d0 10 0 82 80 20 0 82 60 30 0 82 a0 80 0 82
  //   50 a0 0 82 90 40 0 8c f0 ff f0 8d f0 0 0 10 f 0 0 52 b1 10 0 c 20 0 0 8c 20 ff 0 8d 20 0 ff 7 12 10
  //   0 c 70 0 8 a d7 20 0 6 22 20 0 6 11 10 0 6 12 10 0 52 92 0 0 a 28 20 0 c 30 0 0 8c 30 0 ff 8d 30 0 0
  //   2 23 20 0 7 23 20 0 6 11 10 0 6 22 20 0 6 21 10 0 53 b1 10 0 52 a1 0 0 82 80 a0 0 c 20 0 0 8c 20 c0
  //   0 8d 20 0 0 2 12 20 0 c 80 0 18 9 28 30 0 13 c3 0 7 9 2a 30 0 13 c3 0 6 9 27 30 0 13 c3 0 5 13 c2 0
  //   4 12 c3 0 2 a 3a 30 0 6 33 30 0 12 c4 0 3 a 48 40 0 6 44 40 0 6 43 30 0 12 c4 0 1 a 47 40 0 6 44 40
  //   0 12 c5 0 0 6 55 50 0 6 45 40 0 6 33 30 0 6 44 40 0 6 34 30 0 3 23 30 0 9 38 40 0 13 c4 0 b 9 3a 40
  //   0 13 c4 0 a 13 c3 0 8 9 37 30 0 13 c3 0 9 12 c3 0 1 12 c3 0 0 12 c3 0 2 12 c4 0 3 12 c5 0 2 a 5a 50
  //   0 6 55 50 0 12 c6 0 3 a 68 60 0 6 66 60 0 6 65 50 0 12 c6 0 1 a 67 60 0 6 66 60 0 12 c7 0 0 6 77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
endmodule
